// Logisim project d_flip_flop.circ as structural Verilog: 1 circuit, main circuit main
module main (
  input  clock,
  input  D,
  output Q,
  output not_Q
);

  wire nand_1_out, nand_2_out, nand_3_out, nand_4_out;

  nand nand_1 (nand_1_out, nand_4_out, nand_2_out);
  nand nand_2 (nand_2_out, nand_1_out, clock);
  nand nand_3 (nand_3_out, nand_2_out, clock, nand_4_out);
  nand nand_4 (nand_4_out, nand_3_out, D);
  nand nand_5 (Q, nand_2_out, not_Q);
  nand nand_6 (not_Q, Q, nand_3_out);
endmodule
