// Logisim project basis.circ as structural Verilog: 1 circuit, main circuit main
module main (
  input  clear,
  input  Binvert,
  input  [1:0] \Operação 
);

  wire A_out, adder_1_cout, adder_1_out, and_1_out, B_out, Carry_q, clock_1_out, multiplexer_1_out, or_1_out,
       xor_1_out, xor_2_out;
  wire [3:0] A_q3, A_q7, B_q3, B_q7;

  Clock clock_1 (.out(clock_1_out));
  Shift_Register B (
    .in(1'b0), .clk(clock_1_out), .out(B_out), .q0(B_q3[3]), .q1(B_q3[2]), .q2(B_q3[1]), .q3(B_q3[0]),
    .q4(B_q7[3]), .q5(B_q7[2]), .q6(B_q7[1]), .q7(B_q7[0]));  // open: shift, load, clr, d0, d1, d2, d3, d4, d5, d6, d7
  Shift_Register A (
    .in(multiplexer_1_out), .clk(clock_1_out), .out(A_out), .clr(clear), .q0(A_q3[3]), .q1(A_q3[2]),
    .q2(A_q3[1]), .q3(A_q3[0]), .q4(A_q7[3]), .q5(A_q7[2]), .q6(A_q7[1]), .q7(A_q7[0]));  // open: shift, load, d0, d1, d2, d3, d4, d5, d6, d7
  xor xor_1 (xor_1_out, B_out, Binvert);
  Hex_Digit_Display hex_digit_display_1 (.value(A_q7));  // open: dp
  Hex_Digit_Display hex_digit_display_2 (.value(A_q3));  // open: dp
  and and_1 (and_1_out, A_out, B_out);
  or or_1 (or_1_out, A_out, B_out);
  xor xor_2 (xor_2_out, A_out, B_out);
  Hex_Digit_Display hex_digit_display_3 (.value(B_q7));  // open: dp
  Hex_Digit_Display hex_digit_display_4 (.value(B_q3));  // open: dp
  Adder #(.width(1)) adder_1 (.a(A_out), .b(xor_1_out), .out(adder_1_out), .cin(Carry_q), .cout(adder_1_cout));
  D_Flip_Flop Carry (.clk(clock_1_out), .D(adder_1_cout), .Q(Carry_q));  // open: Qn, preset, en, reset
  Multiplexer #(.select(2), .enable("false")) multiplexer_1 (
    .in0(and_1_out), .in1(or_1_out), .in2(xor_2_out), .in3(adder_1_out), .out(multiplexer_1_out),
    .sel(\Operação ));
endmodule
