// Logisim project index.circ as structural Verilog: 5 circuits, main circuit main
module main (
  input  clear,
  input  in_2,
  input  in_3,
  input  Binvert
);

  wire A_out, adder_1_cout, adder_1_out, and_1_out, B_out, Carry_q, clock_1_out, mux_1_output, or_1_out,
       xor_1_out, xor_2_out;
  wire [3:0] A_q3, A_q7, B_q3, B_q7;

  Shift_Register B (
    .in(1'b0), .clk(clock_1_out), .out(B_out), .q0(B_q3[3]), .q1(B_q3[2]), .q2(B_q3[1]), .q3(B_q3[0]),
    .q4(B_q7[3]), .q5(B_q7[2]), .q6(B_q7[1]), .q7(B_q7[0]));  // open: shift, load, clr, d0, d1, d2, d3, d4, d5, d6, d7
  Clock clock_1 (.out(clock_1_out));
  Shift_Register A (
    .in(mux_1_output), .clk(clock_1_out), .out(A_out), .clr(clear), .q0(A_q3[3]), .q1(A_q3[2]), .q2(A_q3[1]),
    .q3(A_q3[0]), .q4(A_q7[3]), .q5(A_q7[2]), .q6(A_q7[1]), .q7(A_q7[0]));  // open: shift, load, d0, d1, d2, d3, d4, d5, d6, d7
  xor xor_1 (xor_1_out, B_out, Binvert);
  Hex_Digit_Display hex_digit_display_1 (.value(A_q7));  // open: dp
  Hex_Digit_Display hex_digit_display_2 (.value(A_q3));  // open: dp
  and and_1 (and_1_out, A_out, B_out);
  or or_1 (or_1_out, A_out, B_out);
  xor xor_2 (xor_2_out, A_out, B_out);
  Hex_Digit_Display hex_digit_display_3 (.value(B_q7));  // open: dp
  Hex_Digit_Display hex_digit_display_4 (.value(B_q3));  // open: dp
  Adder #(.width(1)) adder_1 (.a(A_out), .b(xor_1_out), .out(adder_1_out), .cin(Carry_q), .cout(adder_1_cout));
  D_Flip_Flop Carry (.clk(clock_1_out), .D(adder_1_cout), .Q(Carry_q));  // open: Qn, preset, en, reset
  mux mux_1 (
    .S0(in_2), .S1(in_3), .D0(and_1_out), .D1(or_1_out), .D2(xor_2_out), .D3(adder_1_out),
    .Output(mux_1_output));
endmodule

module registrador (
  input  Clock,
  input  C_In,
  input  Preset_0,
  input  Preset_1,
  input  Preset_2,
  input  Preset_3,
  input  Preset_4,
  input  Preset_5,
  input  Preset_6,
  input  Preset_7,
  input  Clear,
  output C_Out,
  output Q0,
  output Q1,
  output Q2,
  output Q3,
  output Q4,
  output Q5,
  output Q6
);

  D_Flip_Flop d_ff_1 (.clk(Clock), .D(C_In), .Q(Q0), .preset(Preset_0), .reset(Clear));  // open: Qn, en
  D_Flip_Flop d_ff_2 (.clk(Clock), .D(Q0), .Q(Q1), .preset(Preset_1), .reset(Clear));  // open: Qn, en
  D_Flip_Flop d_ff_3 (.clk(Clock), .D(Q1), .Q(Q2), .preset(Preset_2), .reset(Clear));  // open: Qn, en
  D_Flip_Flop d_ff_4 (.clk(Clock), .D(Q2), .Q(Q3), .preset(Preset_3), .reset(Clear));  // open: Qn, en
  D_Flip_Flop d_ff_5 (.clk(Clock), .D(Q3), .Q(Q4), .preset(Preset_4), .reset(Clear));  // open: Qn, en
  D_Flip_Flop d_ff_6 (.clk(Clock), .D(Q4), .Q(Q5), .preset(Preset_5), .reset(Clear));  // open: Qn, en
  D_Flip_Flop d_ff_7 (.clk(Clock), .D(Q5), .Q(Q6), .preset(Preset_6), .reset(Clear));  // open: Qn, en
  D_Flip_Flop d_ff_8 (.clk(Clock), .D(Q6), .Q(C_Out), .preset(Preset_7), .reset(Clear));  // open: Qn, en
endmodule

module mux (
  input  S0,
  input  S1,
  input  D0,
  input  D1,
  input  D2,
  input  D3,
  output Output
);

  wire and_1_out, and_2_out, and_3_out, and_4_out, not_1_out, not_2_out;

  not not_1 (not_1_out, S1);
  not not_2 (not_2_out, S0);
  and and_1 (and_1_out, not_1_out, D0, not_2_out);
  and and_2 (and_2_out, not_1_out, D1, S0);
  and and_3 (and_3_out, S1, D2, not_2_out);
  and and_4 (and_4_out, S1, D3, S0);
  or or_1 (Output, and_1_out, and_2_out, and_3_out, and_4_out);
endmodule

module base (
  input  clear,
  input  Binvert,
  input  [1:0] \Operação 
);

  wire A_out, adder_1_cout, adder_1_out, and_1_out, B_out, Carry_q, clock_1_out, multiplexer_1_out, or_1_out,
       xor_1_out, xor_2_out;
  wire [3:0] A_q3, A_q7, B_q3, B_q7;

  Clock clock_1 (.out(clock_1_out));
  Shift_Register B (
    .in(1'b0), .clk(clock_1_out), .out(B_out), .q0(B_q3[3]), .q1(B_q3[2]), .q2(B_q3[1]), .q3(B_q3[0]),
    .q4(B_q7[3]), .q5(B_q7[2]), .q6(B_q7[1]), .q7(B_q7[0]));  // open: shift, load, clr, d0, d1, d2, d3, d4, d5, d6, d7
  Shift_Register A (
    .in(multiplexer_1_out), .clk(clock_1_out), .out(A_out), .clr(clear), .q0(A_q3[3]), .q1(A_q3[2]),
    .q2(A_q3[1]), .q3(A_q3[0]), .q4(A_q7[3]), .q5(A_q7[2]), .q6(A_q7[1]), .q7(A_q7[0]));  // open: shift, load, d0, d1, d2, d3, d4, d5, d6, d7
  xor xor_1 (xor_1_out, B_out, Binvert);
  Hex_Digit_Display hex_digit_display_1 (.value(A_q3));  // open: dp
  Hex_Digit_Display hex_digit_display_2 (.value(A_q7));  // open: dp
  and and_1 (and_1_out, A_out, B_out);
  or or_1 (or_1_out, A_out, B_out);
  xor xor_2 (xor_2_out, A_out, B_out);
  Hex_Digit_Display hex_digit_display_3 (.value(B_q3));  // open: dp
  Hex_Digit_Display hex_digit_display_4 (.value(B_q7));  // open: dp
  Adder #(.width(1)) adder_1 (.a(A_out), .b(xor_1_out), .out(adder_1_out), .cin(Carry_q), .cout(adder_1_cout));
  D_Flip_Flop Carry (.clk(clock_1_out), .D(adder_1_cout), .Q(Carry_q));  // open: Qn, preset, en, reset
  Multiplexer #(.select(2), .enable("false")) multiplexer_1 (
    .in0(and_1_out), .in1(or_1_out), .in2(xor_2_out), .in3(adder_1_out), .out(multiplexer_1_out),
    .sel(\Operação ));
endmodule

module teste (
  input  clear,
  input  in_2,
  input  in_3,
  input  Binvert
);

  wire A_out, adder_1_cout, adder_1_out, and_1_out, B_out, Carry_q, clock_1_out, mux_1_output, or_1_out,
       xor_1_out, xor_2_out;
  wire [3:0] A_q3, A_q7, B_q3, B_q7;
  wire [7:0] undriven;

  Shift_Register B (
    .in(1'b0), .clk(clock_1_out), .out(B_out), .q0(B_q3[3]), .q1(B_q3[2]), .q2(B_q3[1]), .q3(B_q3[0]),
    .q4(B_q7[3]), .q5(B_q7[2]), .q6(B_q7[1]), .q7(B_q7[0]));  // open: shift, load, clr, d0, d1, d2, d3, d4, d5, d6, d7
  Clock clock_1 (.out(clock_1_out));
  Shift_Register A (
    .in(mux_1_output), .clk(clock_1_out), .out(A_out), .clr(clear), .q0(A_q3[3]), .q1(A_q3[2]), .q2(A_q3[1]),
    .q3(A_q3[0]), .q4(A_q7[3]), .q5(A_q7[2]), .q6(A_q7[1]), .q7(A_q7[0]));  // open: shift, load, d0, d1, d2, d3, d4, d5, d6, d7
  registrador registrador_1 (
    .Preset_0(undriven[7]), .Preset_1(undriven[6]), .Preset_2(undriven[5]), .Preset_3(undriven[4]),
    .Preset_4(undriven[3]), .Preset_5(undriven[2]), .Preset_6(undriven[1]), .Preset_7(undriven[0]));  // open: C_In, Clear, C_Out, Clock, Q0, Q1, Q2, Q3, Q4, Q5, Q6
  xor xor_1 (xor_1_out, B_out, Binvert);
  Hex_Digit_Display hex_digit_display_1 (.value(A_q7));  // open: dp
  Hex_Digit_Display hex_digit_display_2 (.value(A_q3));  // open: dp
  and and_1 (and_1_out, A_out, B_out);
  or or_1 (or_1_out, A_out, B_out);
  xor xor_2 (xor_2_out, A_out, B_out);
  Hex_Digit_Display hex_digit_display_3 (.value(B_q7));  // open: dp
  Hex_Digit_Display hex_digit_display_4 (.value(B_q3));  // open: dp
  Adder #(.width(1)) adder_1 (.a(A_out), .b(xor_1_out), .out(adder_1_out), .cin(Carry_q), .cout(adder_1_cout));
  D_Flip_Flop Carry (.clk(clock_1_out), .D(adder_1_cout), .Q(Carry_q));  // open: Qn, preset, en, reset
  mux mux_1 (
    .S0(in_2), .S1(in_3), .D0(and_1_out), .D1(or_1_out), .D2(xor_2_out), .D3(adder_1_out),
    .Output(mux_1_output));
endmodule
